// Logisim project program10.circ as structural Verilog: 2 circuits, main circuit main
module main (
  input  in_1,
  input  in_2,
  input  in_3,
  output out_4,
  output out_5
);

  wire and_1_out, and_2_out, not_1_out, xor_1_out;

  xor xor_1 (xor_1_out, in_1, in_2);
  and and_1 (and_1_out, in_1, in_2);
  not not_1 (not_1_out, xor_1_out);
  and and_2 (and_2_out, not_1_out, in_3);
  xor xor_2 (out_4, xor_1_out, in_3);
  or or_1 (out_5, and_2_out, and_1_out);
endmodule

module f_a_b_c (
  input  a,
  input  b,
  input  c,
  output f
);

  wire and_1_out, and_2_out, and_3_out, not_1_out, not_2_out, not_3_out;

  not not_1 (not_1_out, a);
  not not_2 (not_2_out, b);
  not not_3 (not_3_out, c);
  and and_1 (and_1_out, not_1_out, not_2_out, c);
  and and_2 (and_2_out, b, not_3_out);
  and and_3 (and_3_out, a, b);
  or or_1 (f, and_1_out, and_2_out, and_3_out);
endmodule
