// Logisim project program2.circ as structural Verilog: 2 circuits, main circuit main
module main (
  input  in_1,
  input  in_2,
  input  in_3,
  input  in_4,
  input  in_5,
  output out_6,
  output out_7,
  output out_8
);

  wire nand_1_out, nand_2_out, nand_3_out;

  nand nand_1 (nand_1_out, in_1, in_2);
  nand nand_2 (nand_2_out, in_3, in_3);
  nand nand_3 (nand_3_out, in_4, in_4);
  nand nand_4 (out_6, nand_1_out, nand_1_out);
  nand nand_5 (out_7, nand_2_out, nand_3_out);
  nand nand_6 (out_8, in_5, in_5, in_5);
endmodule

module F_A_B_C (
  input  A,
  input  B,
  input  C,
  output F
);

  wire and_1_out, not_1_out;

  not not_1 (not_1_out, A);
  and and_1 (and_1_out, not_1_out, B);
  or or_1 (F, C, and_1_out);
endmodule
