// Logisim project program4.circ as structural Verilog: 1 circuit, main circuit main
module main (
  input  in_1,
  input  in_2,
  input  in_3,
  input  in_4,
  input  in_5,
  input  in_6,
  input  in_7,
  input  in_8,
  output out_9,
  output out_10,
  output out_11,
  output out_12
);

  wire and_1_out, not_1_out, not_2_out, not_5_out, not_6_out, not_7_out, not_8_out, or_1_out;

  not not_1 (not_1_out, in_6);
  not not_2 (not_2_out, in_8);
  or or_1 (or_1_out, in_1, in_3);
  and and_1 (and_1_out, not_1_out, not_1_out, not_2_out);
  not not_3 (out_9, or_1_out);
  not not_4 (out_12, and_1_out);
  not not_5 (not_5_out, in_2);
  not not_6 (not_6_out, in_4);
  not not_7 (not_7_out, in_5);
  not not_8 (not_8_out, in_7);
  and and_2 (out_10, not_5_out, not_6_out);
  or or_2 (out_11, not_7_out, not_8_out);
endmodule
