// Logisim project program5.circ as structural Verilog: 3 circuits, main circuit main
module main (
  input  in_1,
  input  in_2,
  input  in_3,
  input  in_4,
  input  in_5,
  input  in_6,
  input  in_7,
  input  in_8,
  input  in_9,
  output out_10,
  output out_11,
  output out_12,
  output out_13,
  output out_14
);

  not not_1 (out_12, in_5);
  or or_1 (out_10, in_1, in_2);
  and and_1 (out_11, in_3, in_4);
  xnor xnor_1 (out_13, in_6, in_7);
  xnor xnor_2 (out_14, in_8, in_9);
endmodule

module F_a_b_c0 (
  input  A,
  input  B,
  input  C,
  output F
);

  wire and_1_out, not_1_out;

  not not_1 (not_1_out, A);
  and and_1 (and_1_out, not_1_out, B);
  or or_1 (F, C, and_1_out);
endmodule

module F_a_b_c (
  input  A,
  input  B,
  input  C,
  output F
);

  wire and_1_out, not_1_out;

  not not_1 (not_1_out, A);
  and and_1 (and_1_out, not_1_out, B);
  or or_1 (F, C, and_1_out);
endmodule
