// Logisim project program6.circ as structural Verilog
module f_a_b_c_d (
  input  a,
  input  b,
  input  c,
  input  d,
  output f
);

  wire and_1_out, and_2_out, and_3_out, and_4_out, and_5_out, not_1_out, not_2_out, or_1_out;

  not not_1 (not_1_out, b);
  not not_2 (not_2_out, d);
  and and_1 (and_1_out, b, c);
  and and_2 (and_2_out, not_1_out, not_2_out);
  and and_3 (and_3_out, and_1_out, d);
  and and_4 (and_4_out, a, b);
  or or_1 (or_1_out, and_2_out, and_3_out);
  and and_5 (and_5_out, and_4_out, d);
  or or_2 (f, or_1_out, and_5_out);
endmodule
